# Fritzing sketch solenoidSorter (saved by Fritzing 0.9.0b)
stripboards: 1

parts:
  Solenoid_L1 = Solenoid
  Q1 = Basic FET N-Channel [package="TO220 [THT]"]
  R1 = Resistor [tolerance=±5% resistance=2.2k package=THT]
  D1 = Diode [package=diode-1n4001]
  Raspberry_Pi_B_rev1 = Raspberry Pi B rev1
  Power_plug1 = Power plug

nets:
  N1: Solenoid_L1.pin1, Q1.drain, D1.A
  N2: Solenoid_L1.pin2, D1.C, Power_plug1.VCC
  N3: Q1.gate, R1.Pin_1
  GND: Q1.source, Raspberry_Pi_B_rev1.GND, Power_plug1.GND
  N4: R1.Pin_0, Raspberry_Pi_B_rev1.GPIO_24
