# Fritzing sketch servoSorter (saved by Fritzing 0.9.0b)
breadboards: 1

parts:
  PWM1 = PCA9685 16x12-bit PWM Breakout
  Servo = Basic Servo
  LED1 = LED - 3mm [color="Red (633nm)" package="3 mm [THT]"]
  Pi1 = Adafruit Pi Cobbler
  R1 = Resistor [tolerance=±5% resistance=330 package="1206 [SMD]"]
  5V_UBEC_Power = Power plug

nets:
  N1: PWM1.no_name_yet#0, Servo.pulse
  N2: PWM1.no_name_yet#1, R1.Pin_1
  N3: PWM1.no_name_yet#100, PWM1.no_name_yet#706, 5V_UBEC_Power.VCC
  N4: PWM1.no_name_yet#603, Pi1.SCL0
  N5: PWM1.no_name_yet#604, Pi1.SDA0
  N6: PWM1.no_name_yet#605, Pi1.3V3
  N7: PWM1.no_name_yet#701, PWM1.no_name_yet#1000, LED1.cathode, 5V_UBEC_Power.GND
  N8: LED1.anode, R1.Pin_0

custom parts:
  Adafruit Pi Cobbler: Adafruit Pi Cobbler GPIO Breakout for Raspberry Pi
