# Fritzing sketch solenoidSorter (saved by Fritzing 0.9.0b)
breadboards: 1

parts:
  Solenoid_L1 = Solenoid
  Q1 = Basic FET N-Channel [package="TO220 [THT]"]
  D1 = Diode [package=diode-1n4001]
  R1 = Resistor [tolerance=±5% resistance=2.2k package=THT]
  Raspberry_Pi_B_rev1 = Raspberry Pi B rev1
  Solenoid_Power = DC Power [voltage=12V]

nets:
  N1: Solenoid_L1.pin1, D1.C
  N2: Solenoid_L1.pin2, Q1.drain, D1.A
  N3: Q1.gate, R1.Pin_1
  N4: R1.Pin_0, Raspberry_Pi_B_rev1.GPIO_0
  N5: Raspberry_Pi_B_rev1.GND, Solenoid_Power.V-
